# Fritzing sketch montage (saved by Fritzing 0.9.3b)

parts:
  Composant1 = Arduino Uno (Rev3)
  S3 = Momentary Switch [package=ksa_sealed_tac_switch]
  Composant2 = Thumb Joystick
  R2 = Resistor [tolerance=±5% resistance=220 package=THT]
  LED2 = RGB LED (com. cathode, rbg) [package="5 mm [THT]"]

nets:
  N1: Composant1.A0, Composant2.HORZ
  N2: Composant1.A1, Composant2.VERT
  GND: Composant1.GND, Composant1.D2, Composant2.GND, R2.Pin_0, LED2.common_cathode
  N3: Composant1.D3_PWM, LED2.red_anode
  N4: Composant1.D5_PWM, LED2.blue_anode
  N5: Composant1.D6_PWM, LED2.green_anode
  5V: Composant1.5V, S3.4, Composant2.VCC
  N6: S3.2, R2.Pin_1
